// Digital circuit 2DisplayDriver.dig as structural Verilog
module _2DisplayDriver (
  input  [5:0] DATA_IN,
  output [6:0] SEG_1,
  output [6:0] SEG_2
);

  SevenSegmentDecoder sevensegmentdecoder_1 (
    .IN_0(DATA_IN[0]), .IN_1(DATA_IN[1]), .IN_2(DATA_IN[2]), .IN_3(DATA_IN[3]), .A(SEG_1[0]), .B(SEG_1[1]),
    .C(SEG_1[2]), .D(SEG_1[3]), .E(SEG_1[4]), .F(SEG_1[5]), .G(SEG_1[6]));
  SevenSegmentDecoder sevensegmentdecoder_2 (
    .IN_0(DATA_IN[4]), .IN_1(DATA_IN[5]), .IN_2(1'b0), .IN_3(1'b0), .A(SEG_2[0]), .B(SEG_2[1]), .C(SEG_2[2]),
    .D(SEG_2[3]), .E(SEG_2[4]), .F(SEG_2[5]), .G(SEG_2[6]));
endmodule
