// Digital circuit ClockDev.dig as structural Verilog
module ClockDev (
  input  EN,
  input  CLR,
  input  CLK,
  output [5:0] SEC,
  output [5:0] MIN,
  output [4:0] HOUR
);

  wire MINUTES_ovf, SECONDS_ovf;

  CounterPreset #(.maxValue(60), .Bits(6)) SECONDS (
    .en(EN), .C(CLK), .dir(1'b0), .in({6{1'b0}}), .ld(1'b0), .clr(CLR), .out(SEC), .ovf(SECONDS_ovf));
  CounterPreset #(.maxValue(60), .Bits(6)) MINUTES (
    .en(SECONDS_ovf), .C(CLK), .dir(1'b0), .in({6{1'b0}}), .ld(1'b0), .clr(CLR), .out(MIN), .ovf(MINUTES_ovf));
  CounterPreset #(.maxValue(24), .Bits(5)) HOURS (
    .en(MINUTES_ovf), .C(CLK), .dir(1'b0), .in({5{1'b0}}), .ld(1'b0), .clr(CLR), .out(HOUR));  // open: ovf
endmodule
