// Digital circuit DigitalAlarm.dig as structural Verilog
module DigitalAlarm (
  input  CLK,
  input  INC,
  input  SET,
  input  CLR,
  output MIN_SEG_2_A,
  output MIN_SEG_2B,
  output MIN_SEG_2C,
  output MIN_SEG_2D,
  output MIN_SEG_2E,
  output MIN_SEG_2F,
  output MIN_SEG_2G,
  output MIN_SEG_1A,
  output MIN_SEG_1B,
  output MIN_SEG_1C,
  output MIN_SEG_1D,
  output MIN_SEG_1E,
  output MIN_SEG_1F,
  output MIN_SEG_1G,
  output SEC_SEG_2_A,
  output SEC_SEG_2B,
  output SEC_SEG_2C,
  output SEC_SEG_2D,
  output SEC_SEG_2E,
  output SEC_SEG_2F,
  output SEC_SEG_2G,
  output SEC_SEG_1A,
  output SEC_SEG_1B,
  output SEC_SEG_1C,
  output SEC_SEG_1D,
  output SEC_SEG_1E,
  output SEC_SEG_1F,
  output SEC_SEG_1G,
  output HOUR_SEG_2_A,
  output HOUR_SEG_2B,
  output HOUR_SEG_2C,
  output HOUR_SEG_2D,
  output HOUR_SEG_2E,
  output HOUR_SEG_2F,
  output HOUR_SEG_2G,
  output HOUR_SEG_1A,
  output HOUR_SEG_1B,
  output HOUR_SEG_1C,
  output HOUR_SEG_1D,
  output HOUR_SEG_1E,
  output HOUR_SEG_1F,
  output HOUR_SEG_1G
);

  wire and_1_out, and_2_out, or_1_out;
  wire [4:0] clockdev_1_hour;
  wire [5:0] clockdev_1_min, clockdev_1_sec;

  and and_1 (and_1_out, CLK, ~SET);  // And
  and and_2 (and_2_out, SET, INC);
  or or_1 (or_1_out, and_1_out, and_2_out);
  ClockDev clockdev_1 (
    .EN(1'b1), .CLR(CLR), .CLK(or_1_out), .SEC(clockdev_1_sec), .MIN(clockdev_1_min), .HOUR(clockdev_1_hour));
  SevenSegmentDecoder sevensegmentdecoder_1 (
    .IN_0(clockdev_1_sec[0]), .IN_1(clockdev_1_sec[1]), .IN_2(clockdev_1_sec[2]), .IN_3(clockdev_1_sec[3]),
    .A(SEC_SEG_2_A), .B(SEC_SEG_2B), .C(SEC_SEG_2C), .D(SEC_SEG_2D), .E(SEC_SEG_2E), .F(SEC_SEG_2F),
    .G(SEC_SEG_2G));
  SevenSegmentDecoder sevensegmentdecoder_2 (
    .IN_0(clockdev_1_sec[3]), .IN_1(clockdev_1_sec[4]), .IN_2(clockdev_1_sec[5]), .IN_3(1'b0),
    .A(SEC_SEG_1A), .B(SEC_SEG_1B), .C(SEC_SEG_1C), .D(SEC_SEG_1D), .E(SEC_SEG_1E), .F(SEC_SEG_1F),
    .G(SEC_SEG_1G));
  SevenSegmentDecoder sevensegmentdecoder_3 (
    .IN_0(clockdev_1_min[0]), .IN_1(clockdev_1_min[1]), .IN_2(clockdev_1_min[2]), .IN_3(clockdev_1_min[3]),
    .A(MIN_SEG_2_A), .B(MIN_SEG_2B), .C(MIN_SEG_2C), .D(MIN_SEG_2D), .E(MIN_SEG_2E), .F(MIN_SEG_2F),
    .G(MIN_SEG_2G));
  SevenSegmentDecoder sevensegmentdecoder_4 (
    .IN_0(clockdev_1_min[3]), .IN_1(clockdev_1_min[4]), .IN_2(clockdev_1_min[5]), .IN_3(1'b0),
    .A(MIN_SEG_1A), .B(MIN_SEG_1B), .C(MIN_SEG_1C), .D(MIN_SEG_1D), .E(MIN_SEG_1E), .F(MIN_SEG_1F),
    .G(MIN_SEG_1G));
  SevenSegmentDecoder sevensegmentdecoder_5 (
    .IN_0(clockdev_1_hour[0]), .IN_1(clockdev_1_hour[1]), .IN_2(clockdev_1_hour[2]),
    .IN_3(clockdev_1_hour[3]), .A(HOUR_SEG_2_A), .B(HOUR_SEG_2B), .C(HOUR_SEG_2C), .D(HOUR_SEG_2D),
    .E(HOUR_SEG_2E), .F(HOUR_SEG_2F), .G(HOUR_SEG_2G));
  SevenSegmentDecoder sevensegmentdecoder_6 (
    .IN_0(clockdev_1_hour[3]), .IN_1(clockdev_1_hour[4]), .IN_2(1'b0), .IN_3(1'b0), .A(HOUR_SEG_1A),
    .B(HOUR_SEG_1B), .C(HOUR_SEG_1C), .D(HOUR_SEG_1D), .E(HOUR_SEG_1E), .F(HOUR_SEG_1F), .G(HOUR_SEG_1G));

  // Notes on the sheet:
  //   CLK: Hz: 100
endmodule
