// Digital circuit SevenSegmentDecoder.dig as structural Verilog
module SevenSegmentDecoder (
  input  IN_0,
  input  IN_1,
  input  IN_2,
  input  IN_3,
  output A,
  output B,
  output C,
  output D,
  output E,
  output F,
  output G
);

  LookUpTable #(.Bits(7)) DECODER (.in0(IN_0), .in1(IN_1), .in2(IN_2), .in3(IN_3), .out({A, B, C, D, E, F, G}));

  // Notes on the sheet:
  //   contents of DECODER (hex, n*v repeats v):
  //   7e,30,6d,79,33,5b,5f,70,7f,7b,77,1f,4e,3d,4f,47
endmodule
